# Fritzing sketch Bluetooth (saved by Fritzing 0.9.3b)
breadboards: 1

parts:
  U1 = WS2812 RGB LED strip
  o1 = Module display OLED I2C 128x64 SSD1306 [package=THT]
  LED1 = RGB LED (com. cathode, rbg) [package="5 mm [THT]"]
  Parça1 = Bluetooth HC-05 Macho
  Parça2 = Arduino Uno (Rev3) - ICSP
  R1 = Resistor [tolerance=±5% resistance=1k package=THT]
  R2 = Resistor [tolerance=±5% resistance=1k package=THT]
  R3 = Resistor [tolerance=±5% resistance=1k package=THT]

nets:
  GND: U1.GND, o1.GND, LED1.common_cathode, Parça1.GND, Parça2.GND
  VCC: U1.VCC, Parça1.VCC, Parça2.5V
  N1: U1.DOUT, Parça2.D12/MISO
  VCC_2: o1.VCC, Parça2.3V3
  N2: o1.SCL, Parça2.A5/SCL
  N3: o1.SDA, Parça2.A4/SDA
  N4: LED1.red_anode, R2.Pin_0
  N5: LED1.blue_anode, R3.Pin_0
  N6: LED1.green_anode, R1.Pin_0
  N7: Parça1.TXD, Parça2.D0/RX
  N8: Parça1.RXD, Parça2.D1/TX
  N9: Parça2.D8, R2.Pin_1
  N10: Parça2.D10_PWM/SS, R3.Pin_1
  N11: Parça2.D11_PWM/MOSI, R1.Pin_1

custom parts:
  WS2812 RGB LED strip: WS2812 strip
  Module display OLED I2C 128x64 SSD1306: Ecran OLED I2C SSD163 de 128x64 avec connexion I2C
